# Fritzing sketch Untitled Sketch 2 (saved by Fritzing 0.9.3b)

parts:
  Part2 = Adafruit FeatherWing Proto [part_number="Adafruit #2884"]
  DOTSTAR1 = DotStar Strip -- Black (60/m) [part_number=2239]
  R1 = Rotary Potentiometer (Small) [maximum_resistance=100kΩ package=THT]
  S1 = Pushbutton [package="[THT]"]
  S2 = Pushbutton [package="[THT]"]
  S3 = Pushbutton [package="[THT]"]
  S4 = Pushbutton [package="[THT]"]
  S5 = Pushbutton [package="[THT]"]
  S6 = Pushbutton [package="[THT]"]
  S7 = Taiway 100-SP-X-T1 SPDT Miniature Toggle Switch [part_number=100-SP-X-T1-0-0-B1-M1 package=THT]
  LED1 = LED - 5mm [color="Red (633nm)" package="5 mm [THT]"]
  LED2 = LED - 5mm [color="Red (633nm)" package="5 mm [THT]"]
  LED3 = LED - 5mm [color="Red (633nm)" package="5 mm [THT]"]
  LED4 = LED - 5mm [color="Red (633nm)" package="5 mm [THT]"]
  LED5 = LED - 5mm [color="Red (633nm)" package="5 mm [THT]"]
  LED6 = LED - 5mm [color="Red (633nm)" package="5 mm [THT]"]
  S8 = Toggle Switch [package=THT]
  R2 = Resistor [tolerance=±5% resistance=220 package=THT]

nets:
  N1: Part2.VBAT, DOTSTAR1.+5V
  GND: Part2.N, Part2.F, Part2.E, Part2.D, Part2.C, Part2.B, Part2.GND, DOTSTAR1.GND, R1.leg2, S1.Pin_3, S1.Pin_4, S2.Pin_3, S2.Pin_4, S3.Pin_3, S3.Pin_4, S4.Pin_3, S4.Pin_4, S5.Pin_3, S5.Pin_4, S6.Pin_3, S6.Pin_4, S7.L2, LED1.cathode, LED2.cathode, LED3.cathode, LED4.cathode, LED5.cathode, LED6.cathode, S8.L1
  N2: Part2.M, LED1.anode
  N3: Part2.L, LED2.anode
  N4: Part2.K, LED3.anode
  N5: Part2.J, LED4.anode
  N6: Part2.I, LED5.anode
  N7: Part2.H, LED6.anode
  N8: Part2.SCL, S7.L1
  N9: Part2.MOSI, DOTSTAR1.DI
  N10: Part2.SCK, DOTSTAR1.CI
  N11: Part2.A, R1.wiper
  N12: Part2.3V, R2.Pin_0
  N13: Part2.SDA, S8.COM
  N14: R1.leg1, R2.Pin_1

custom parts:
  Adafruit FeatherWing Proto: This is the FeatherWing Proto - a prototyping add-on for all Feather boards. Using our Feather Stacking Headers or Feather Female Headers you can connect a FeatherWing on top or bottom of your Feather board and let the board take flight! This has a duplicate breakout for each pin on a Feather, as well as a bunch of plain grid proto holes. For GND and 3.3V, we give you a strip of connected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
  DotStar Strip -- Black (60/m): NeopixelDotStar Strip, Black, 60 pixels per meter.
